// Logisim project BasicGates.circ as structural Verilog: 1 circuit, main circuit main
// CD4007 Logic Gates
module main (
  input  _6,
  input  _3,
  input  _10,
  input  _6_2,
  input  _6_3,
  input  _3_2,
  input  _3_3,
  input  _10_2,
  input  _10_3,
  input  _3_4,
  input  _3_5,
  input  _10_4,
  input  _6_4,
  input  _3_6,
  input  _3_7,
  input  _10_5,
  input  _6_5,
  output _8_13,
  output _1_5,
  output _12,
  output _12_2,
  output _1_5_8,
  output _1_12,
  output _8_13_2,
  output _1_12_13,
  output _5_8_12
);

  wire transistor_3_out, transistor_8_out, transistor_9_out, transistor_10_out, transistor_19_out,
       transistor_20_out, transistor_22_out, transistor_24_out, transistor_29_out, transistor_30_out;

  Transistor transistor_1 (.in(1'b1), .out(_8_13), .gate(_6));
  Transistor #(.\type ("n")) transistor_2 (.in(1'b0), .out(_8_13), .gate(_6));
  Transistor transistor_3 (.in(1'b1), .out(transistor_3_out), .gate(_6_2));
  Transistor transistor_4 (.in(transistor_3_out), .out(_1_5_8), .gate(_3_2));
  Transistor #(.\type ("n")) transistor_5 (.in(1'b0), .out(_1_5_8), .gate(_6_2));
  Transistor transistor_6 (.in(1'b1), .out(_1_12), .gate(_10_2));
  Transistor #(.\type ("n")) transistor_7 (.in(transistor_8_out), .out(_1_12), .gate(_10_2));
  Transistor #(.\type ("n")) transistor_8 (.in(1'b0), .out(transistor_8_out), .gate(_3_4));
  Transistor transistor_9 (.in(1'b1), .out(transistor_9_out), .gate(_6_4));
  Transistor transistor_10 (.in(transistor_9_out), .out(transistor_10_out), .gate(_3_6));
  Transistor transistor_11 (.in(transistor_10_out), .out(_5_8_12), .gate(_10_5));
  Transistor #(.\type ("n")) transistor_12 (.in(1'b0), .out(_5_8_12), .gate(_6_4));
  Transistor #(.\type ("n")) transistor_13 (.in(1'b0), .out(_1_5_8), .gate(_3_2));
  Transistor transistor_14 (.in(1'b1), .out(_1_12), .gate(_3_4));
  Transistor #(.\type ("n")) transistor_15 (.in(1'b0), .out(_5_8_12), .gate(_3_6));
  Transistor #(.\type ("n")) transistor_16 (.in(1'b0), .out(_5_8_12), .gate(_10_5));
  Transistor transistor_17 (.in(1'b1), .out(_1_5), .gate(_3));
  Transistor #(.\type ("n")) transistor_18 (.in(1'b0), .out(_1_5), .gate(_3));
  Transistor transistor_19 (.in(1'b1), .out(transistor_19_out), .gate(_6_3));
  Transistor transistor_20 (.in(transistor_19_out), .out(transistor_20_out), .gate(_3_3));
  Transistor #(.\type ("n")) transistor_21 (.in(1'b0), .out(transistor_20_out), .gate(_6_3));
  Transistor transistor_22 (.in(1'b1), .out(transistor_22_out), .gate(_10_3));
  Transistor #(.\type ("n")) transistor_23 (.in(transistor_24_out), .out(transistor_22_out), .gate(_10_3));
  Transistor #(.\type ("n")) transistor_24 (.in(1'b0), .out(transistor_24_out), .gate(_3_5));
  Transistor #(.\type ("n")) transistor_25 (.in(1'b0), .out(transistor_20_out), .gate(_3_3));
  Transistor transistor_26 (.in(1'b1), .out(transistor_22_out), .gate(_3_5));
  Transistor transistor_27 (.in(1'b1), .out(_1_12_13), .gate(_10_4));
  Transistor #(.\type ("n")) transistor_28 (.in(transistor_29_out), .out(_1_12_13), .gate(_10_4));
  Transistor #(.\type ("n")) transistor_29 (.in(transistor_30_out), .out(transistor_29_out), .gate(_3_7));
  Transistor #(.\type ("n")) transistor_30 (.in(1'b0), .out(transistor_30_out), .gate(_6_5));
  Transistor transistor_31 (.in(1'b1), .out(_12_2), .gate(transistor_20_out));
  Transistor #(.\type ("n")) transistor_32 (.in(1'b0), .out(_12_2), .gate(transistor_20_out));
  Transistor transistor_33 (.in(1'b1), .out(_8_13_2), .gate(transistor_22_out));
  Transistor #(.\type ("n")) transistor_34 (.in(1'b0), .out(_8_13_2), .gate(transistor_22_out));
  Transistor transistor_35 (.in(1'b1), .out(_1_12_13), .gate(_3_7));
  Transistor transistor_36 (.in(1'b1), .out(_12), .gate(_10));
  Transistor #(.\type ("n")) transistor_37 (.in(1'b0), .out(_12), .gate(_10));
  Transistor transistor_38 (.in(1'b1), .out(_1_12_13), .gate(_6_5));

  // Notes on the sheet:
  //   14
  //   7
  //   14
  //   2,13
  //   7
  //   2-INPUT NOR
  //   11
  //   5,9
  //   4
  //   2-INPUT NAND
  //   14
  //   2,13
  //   1,11
  //   7
  //   3-INPUT NOR
  //   4
  //   2
  //   4
  //   9
  //   2
  //   4
  //   NOT (INVERTER)
  //   CD4007 Logic Gate Connections
  //   14
  //   2,13
  //   7
  //   11
  //   5,9
  //   4
  //   1,5,8,10
  //   4
  //   2-INPUT OR
  //   2
  //   1,6,12
  //   2-INPUT AND
  //   11
  //   5,9
  //   4,8
  //   7
  //   3-INPUT NAND
  //   11
  //   9
  //   14
  //   7
  //   2
  //   11
  //   9
  //   14
endmodule
