// Logisim project CD4007 Logic.circ as structural Verilog: 1 circuit, main circuit main
module main (
  input  PIN_14,
  input  PIN_2,
  input  PIN_11,
  input  PIN_6,
  input  PIN_3,
  input  PIN_10,
  input  PIN_7,
  input  PIN_4,
  input  PIN_9,
  output PIN_13,
  output PIN_1,
  output PIN_12,
  output PIN_8,
  output PIN_5
);

  Transistor transistor_1 (.in(PIN_14), .out(PIN_13), .gate(PIN_6));
  Transistor #(.\type ("n")) transistor_2 (.in(PIN_7), .out(PIN_8), .gate(PIN_6));
  Transistor transistor_3 (.in(PIN_2), .out(PIN_1), .gate(PIN_3));
  Transistor #(.\type ("n")) transistor_4 (.in(PIN_4), .out(PIN_5), .gate(PIN_3));
  Transistor transistor_5 (.in(PIN_11), .out(PIN_12), .gate(PIN_10));
  Transistor #(.\type ("n")) transistor_6 (.in(PIN_9), .out(PIN_12), .gate(PIN_10));

  // Notes on the sheet:
  //   Connect to 5V
  //   Connect to GND
  //   CD4007 Dual Complementary Pair Plus Inverter
endmodule
