// Logisim project CD4030ExclusiveOR.circ as structural Verilog: 1 circuit, main circuit main
module main (
  input  a,
  input  b,
  output y
);

  wire transistor_1_out, transistor_3_out, transistor_5_out, transistor_6_out;

  Transistor transistor_1 (.in(1'b1), .out(transistor_1_out), .gate(a));
  Transistor #(.\type ("n")) transistor_2 (.in(1'b0), .out(transistor_1_out), .gate(a));
  Transistor transistor_3 (.in(1'b1), .out(transistor_3_out), .gate(b));
  Transistor #(.\type ("n")) transistor_4 (.in(1'b0), .out(transistor_3_out), .gate(b));
  Transistor transistor_5 (.in(1'b1), .out(transistor_5_out), .gate(transistor_3_out));
  Transistor transistor_6 (.in(transistor_5_out), .out(transistor_6_out), .gate(transistor_1_out));
  Transistor #(.\type ("n")) transistor_7 (.in(transistor_1_out), .out(transistor_6_out), .gate(transistor_3_out));
  Transistor transistor_8 (.in(transistor_3_out), .out(transistor_6_out), .gate(a));
  Transistor #(.\type ("n")) transistor_9 (.in(transistor_3_out), .out(transistor_6_out), .gate(transistor_1_out));
  Transistor transistor_10 (.in(1'b1), .out(y), .gate(transistor_6_out));
  Transistor #(.\type ("n")) transistor_11 (.in(1'b0), .out(y), .gate(transistor_6_out));

  // Notes on the sheet:
  //   CD4030 Exclusive-OR
endmodule
