// Logisim project TriStateInverter.circ as structural Verilog: 1 circuit, main circuit main
module main (
  input  _10,
  input  in_2,
  input  _6,
  input  in_4,
  output _12,
  output out_6
);

  wire transistor_1_out, transistor_3_out, transistor_6_out, transistor_7_out, transistor_9_out,
       transistor_12_out;

  Transistor transistor_1 (.in(1'b1), .out(transistor_1_out), .gate(in_4));
  Transistor #(.\type ("n")) transistor_2 (.in(1'b0), .out(transistor_1_out), .gate(in_4));
  Transistor transistor_3 (.in(1'b1), .out(transistor_3_out), .gate(in_4));
  Transistor transistor_4 (.in(transistor_3_out), .out(out_6), .gate(in_2));
  Transistor #(.\type ("n")) transistor_5 (.in(transistor_6_out), .out(out_6), .gate(in_2));
  Transistor #(.\type ("n")) transistor_6 (.in(1'b0), .out(transistor_6_out), .gate(transistor_1_out));
  Transistor transistor_7 (.in(1'b1), .out(transistor_7_out), .gate(_6));
  Transistor #(.\type ("n")) transistor_8 (.in(1'b0), .out(transistor_7_out), .gate(_6));
  Transistor transistor_9 (.in(1'b1), .out(transistor_9_out), .gate(_6));
  Transistor transistor_10 (.in(transistor_9_out), .out(_12), .gate(_10));
  Transistor #(.\type ("n")) transistor_11 (.in(transistor_12_out), .out(_12), .gate(_10));
  Transistor #(.\type ("n")) transistor_12 (.in(1'b0), .out(transistor_12_out), .gate(transistor_7_out));

  // Notes on the sheet:
  //   TRI-STATE INVERTING BUFFER
  //   TRI-STATE Control 
  //   14
  //   7
  //   3,8,13
  //   TRI-STATE INVERTING BUFFER
  //   2
  //   1,11
  //   5,9
  //   4
endmodule
