// Logisim project Universality.circ as structural Verilog: 1 circuit, main circuit main
module main (
  input  in_1,
  input  in_2,
  input  in_3,
  input  in_4,
  input  in_5,
  input  in_6,
  input  in_7,
  input  in_8,
  input  in_9,
  input  in_10,
  output out_11,
  output out_12,
  output out_13,
  output out_14,
  output out_15,
  output out_16
);

  wire transistor_3_out, transistor_4_out, transistor_6_out, transistor_7_out, transistor_9_out,
       transistor_10_out, transistor_12_out, transistor_19_out, transistor_22_out, transistor_25_out,
       transistor_29_out, transistor_30_out, transistor_33_out, transistor_34_out, transistor_37_out,
       transistor_38_out, transistor_41_out, transistor_45_out;

  Transistor transistor_1 (.in(1'b1), .out(out_11), .gate(in_1));
  Transistor #(.\type ("n")) transistor_2 (.in(transistor_3_out), .out(out_11), .gate(in_1));
  Transistor #(.\type ("n")) transistor_3 (.in(1'b0), .out(transistor_3_out), .gate(in_1));
  Transistor transistor_4 (.in(1'b1), .out(transistor_4_out), .gate(in_3));
  Transistor #(.\type ("n")) transistor_5 (.in(transistor_6_out), .out(transistor_4_out), .gate(in_3));
  Transistor #(.\type ("n")) transistor_6 (.in(1'b0), .out(transistor_6_out), .gate(in_5));
  Transistor transistor_7 (.in(1'b1), .out(transistor_7_out), .gate(in_7));
  Transistor #(.\type ("n")) transistor_8 (.in(transistor_9_out), .out(transistor_7_out), .gate(in_7));
  Transistor #(.\type ("n")) transistor_9 (.in(1'b0), .out(transistor_9_out), .gate(in_7));
  Transistor transistor_10 (.in(1'b1), .out(transistor_10_out), .gate(in_9));
  Transistor #(.\type ("n")) transistor_11 (.in(transistor_12_out), .out(transistor_10_out), .gate(in_9));
  Transistor #(.\type ("n")) transistor_12 (.in(1'b0), .out(transistor_12_out), .gate(in_9));
  Transistor transistor_13 (.in(1'b1), .out(out_11), .gate(in_1));
  Transistor transistor_14 (.in(1'b1), .out(transistor_4_out), .gate(in_5));
  Transistor transistor_15 (.in(1'b1), .out(transistor_7_out), .gate(in_7));
  Transistor transistor_16 (.in(1'b1), .out(transistor_10_out), .gate(in_9));
  Transistor transistor_17 (.in(1'b1), .out(out_13), .gate(transistor_4_out));
  Transistor #(.\type ("n")) transistor_18 (.in(transistor_19_out), .out(out_13), .gate(transistor_4_out));
  Transistor #(.\type ("n")) transistor_19 (.in(1'b0), .out(transistor_19_out), .gate(transistor_4_out));
  Transistor transistor_20 (.in(1'b1), .out(out_15), .gate(transistor_7_out));
  Transistor #(.\type ("n")) transistor_21 (.in(transistor_22_out), .out(out_15), .gate(transistor_7_out));
  Transistor #(.\type ("n")) transistor_22 (.in(1'b0), .out(transistor_22_out), .gate(transistor_10_out));
  Transistor transistor_23 (.in(1'b1), .out(out_13), .gate(transistor_4_out));
  Transistor transistor_24 (.in(1'b1), .out(out_15), .gate(transistor_10_out));
  Transistor transistor_25 (.in(1'b1), .out(transistor_25_out), .gate(in_2));
  Transistor transistor_26 (.in(transistor_25_out), .out(out_12), .gate(in_2));
  Transistor #(.\type ("n")) transistor_27 (.in(1'b0), .out(out_12), .gate(in_2));
  Transistor #(.\type ("n")) transistor_28 (.in(1'b0), .out(out_12), .gate(in_2));
  Transistor transistor_29 (.in(1'b1), .out(transistor_29_out), .gate(in_4));
  Transistor transistor_30 (.in(transistor_29_out), .out(transistor_30_out), .gate(in_6));
  Transistor #(.\type ("n")) transistor_31 (.in(1'b0), .out(transistor_30_out), .gate(in_6));
  Transistor #(.\type ("n")) transistor_32 (.in(1'b0), .out(transistor_30_out), .gate(in_4));
  Transistor transistor_33 (.in(1'b1), .out(transistor_33_out), .gate(in_8));
  Transistor transistor_34 (.in(transistor_33_out), .out(transistor_34_out), .gate(in_8));
  Transistor #(.\type ("n")) transistor_35 (.in(1'b0), .out(transistor_34_out), .gate(in_8));
  Transistor #(.\type ("n")) transistor_36 (.in(1'b0), .out(transistor_34_out), .gate(in_8));
  Transistor transistor_37 (.in(1'b1), .out(transistor_37_out), .gate(in_10));
  Transistor transistor_38 (.in(transistor_37_out), .out(transistor_38_out), .gate(in_10));
  Transistor #(.\type ("n")) transistor_39 (.in(1'b0), .out(transistor_38_out), .gate(in_10));
  Transistor #(.\type ("n")) transistor_40 (.in(1'b0), .out(transistor_38_out), .gate(in_10));
  Transistor transistor_41 (.in(1'b1), .out(transistor_41_out), .gate(transistor_30_out));
  Transistor transistor_42 (.in(transistor_41_out), .out(out_14), .gate(transistor_30_out));
  Transistor #(.\type ("n")) transistor_43 (.in(1'b0), .out(out_14), .gate(transistor_30_out));
  Transistor #(.\type ("n")) transistor_44 (.in(1'b0), .out(out_14), .gate(transistor_30_out));
  Transistor transistor_45 (.in(1'b1), .out(transistor_45_out), .gate(transistor_34_out));
  Transistor transistor_46 (.in(transistor_45_out), .out(out_16), .gate(transistor_38_out));
  Transistor #(.\type ("n")) transistor_47 (.in(1'b0), .out(out_16), .gate(transistor_34_out));
  Transistor #(.\type ("n")) transistor_48 (.in(1'b0), .out(out_16), .gate(transistor_38_out));

  // Notes on the sheet:
  //   2-INPUT NAND
  //   INVERTER
  //   2-INPUT NAND
  //   2-INPUT NAND
  //   2-INPUT NAND
  //   2-INPUT AND
  //   2-INPUT OR
  //   2-INPUT NAND
  //   2-INPUT NAND
  //   Universality of NAND and NOR gates
  //   2-INPUT NOR
  //   INVERTER
  //   2-INPUT NOR
  //   2-INPUT NOR
  //   2-INPUT NOR
  //   2-INPUT OR
  //   2-INPUT AND
  //   2-INPUT NOR
  //   2-INPUT NOR
endmodule
